# Fritzing sketch micronova (saved by Fritzing 0.9.4)
circuit board: 5.95448cm x 5.75073cm
breadboards: 1

parts:
  En = Sharp PC817 [package=THT]
  510 = Resistor [tolerance=±5% resistance=510 package=THT]
  RX = Sharp PC817 [package=THT]
  510_2 = Resistor [tolerance=±5% resistance=510 package=THT]
  510_3 = Resistor [tolerance=±5% resistance=510 package=THT]
  RESET = Pushbutton [package="[THT]"]
  TX = Sharp PC817 [package=THT]
  7805 = Voltage Regulator [package=78xxl]
  J1 = generic 4 pos screw terminal [package=THT]
  220 = Resistor [tolerance=±5% resistance=220 package=THT]
  RED = LED - 5mm [color="Red (633nm)" package="5 mm [THT]"]
  En_5V = female pin header, 2 pins [form="♀ (female)"]
  M1 = DOIT Esp32 DevKit v1 (30 pins long, 11 pins width) [part_number=ESP32S-PIN30]

nets:
  N1: En.Pin_1, TX.Pin_1, M1.3V3
  N2: En.Pin_2, 510_3.Pin_1
  N3: En.Pin_4, J1.pin1, En_5V.pin1
  N4: En.Pin_3, RX.Pin_1
  N5: 510.Pin_0, M1.TX2
  N6: 510.Pin_1, TX.Pin_2
  N7: RX.Pin_2, 510_2.Pin_0
  N8: RX.Pin_4, M1.RX2
  GND: RX.Pin_3, RESET.Pin_3, RESET.Pin_4, TX.Pin_3, 7805.GND, J1.pin3, 220.Pin_1, M1.GND
  N9: 510_2.Pin_1, TX.Pin_4, J1.pin2
  N10: 510_3.Pin_0, M1.D18
  N11: RESET.Pin_2, M1.D13
  N12: 7805.IN, J1.pin4
  N13: 7805.OUT, En_5V.pin2, M1.VIN
  N14: 220.Pin_0, RED.cathode
  N15: RED.anode, M1.D14

notes:
  GND
  SERIAL
  5V
  20V
  DATA
  NETDATA Palletheater v1.1
  13 | Switch
  14 | LED
  TX | 17
  RX | 16
  VIN
  Enable RX | 18
  2022
  LED | 14
  Switch | 13
  16 | RX
  17 | TX
  18 |  Enable RX
  ESP32 dev Board
  NETDATA Palletheater v1.1 - 2022

custom parts:
  generic 4 pos screw terminal: generic 4 pin 5.08mm (0.2") Pitch screw Terminal, 4 pole Fritzing part is derived from Screw terminals by Lionel Michel.
  DOIT Esp32 DevKit v1 (30 pins long, 11 pins width): The DOIT Esp32 DevKit v1 is one of the development board created by DOIT to evaluate the ESP-WROOM-32 module. It is based on the ESP32 microcontroller that boasts Wifi, Bluetooth, Ethernet and Low Power support all in a single chip. (vanepp) made breadboard work, adjusted pin numbering and labels and reduced size of schematic and cleaned up pcb. This chip is 30pins long (2 x15) and 11 pins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
